# Fritzing sketch ubicomp circuit (saved by Fritzing 0.9.3b)
breadboards: 1

parts:
  IC1 = AD8232 HeartRate Monitor [part_number=SEN-12650 chip_label=IC package="DIP (Dual Inline) [THT]"]
  Part1 = Arduino MKR1000
  PIR1 = PIR sensor
  8x8_LED_Modul_mit_MAX1 = 8x8 LED Modul mit MAX7219 [package=THT]
  BuzzerDFR1 = BuzzerDFR0032

nets:
  GND: IC1.GND, Part1.GND, PIR1.GND, BuzzerDFR1.GND
  3.3V: IC1.3.3v, Part1.VCC, PIR1.VDD, 8x8_LED_Modul_mit_MAX1.VCC_Eingang, 8x8_LED_Modul_mit_MAX1.GND_Eingang, BuzzerDFR1.5V
  N1: IC1.OUTPUT, Part1.A0_DAC0
  N2: IC1.LO-, Part1.D9_SCK
  N3: IC1.LO+, Part1.D8_MOSI
  N4: Part1.D2_PWM, PIR1.SIG
  N5: Part1.D10_MISO, 8x8_LED_Modul_mit_MAX1.CLK_Eingang
  N6: Part1.D11_SDA, 8x8_LED_Modul_mit_MAX1.CS_Eingang
  N7: Part1.D12_SCL, 8x8_LED_Modul_mit_MAX1.DIN_Eingang
  N8: Part1.14_TX, BuzzerDFR1.Signal

custom parts:
  AD8232 HeartRate Monitor: A DIP stand-in part for whatever IC you want. With 10 pins on a 600mil dual inline package (DIP) footprint.
  Arduino MKR1000: MKR1000 is a powerful board that combines the functionality of the Zero and the Wi-Fi Shield. It is the ideal solution for makers wanting to design IoT projects with minimal previous experience in networking
